// Logisim project ProjetoJeffDjumay.circ as structural Verilog: 4 circuits, main circuit main
module main (
  input  in_1,
  input  in_2,
  input  in_3,
  input  in_4,
  input  in_5,
  input  in_6
);

  wire modulo2_1_da, modulo2_1_sai, modulo3_1_empate, modulo3_1_vencedorjogador2,
       modulo3_1_vencedorjogardor1, moduloi_1_s0, moduloi_1_s1, moduloi_2_s0, moduloi_2_s1;

  ModuloI moduloi_1 (.pedra(in_1), .papel(in_2), .tesoura(in_3), .S0(moduloi_1_s0), .S1(moduloi_1_s1));
  ModuloI moduloi_2 (.pedra(in_4), .papel(in_5), .tesoura(in_6), .S0(moduloi_2_s0), .S1(moduloi_2_s1));
  Modulo2 modulo2_1 (
    .Jog(moduloi_1_s0), .I(moduloi_1_s1), .Joga(moduloi_2_s0), .II(moduloi_2_s1), .Sai(modulo2_1_sai),
    .da(modulo2_1_da));
  LED Jogador1 (.in(modulo3_1_vencedorjogardor1));
  LED Jogador2 (.in(modulo3_1_vencedorjogador2));
  Modulo3 modulo3_1 (
    .a(modulo2_1_sai), .b(modulo2_1_da), .VencedorJogardor1(modulo3_1_vencedorjogardor1),
    .VencedorJogador2(modulo3_1_vencedorjogador2), .Empate(modulo3_1_empate));
  LED Empate (.in(modulo3_1_empate));

  // Notes on the sheet:
  //   Jogador1
  //   Jogador2
endmodule

module ModuloI (
  input  pedra,
  input  papel,
  input  tesoura,
  output S0,
  output S1
);

  wire and_1_out, and_2_out, and_3_out, and_4_out, not_1_out, not_2_out, not_3_out;

  not not_1 (not_1_out, pedra);
  not not_2 (not_2_out, papel);
  not not_3 (not_3_out, tesoura);
  and and_1 (and_1_out, not_1_out, not_2_out, tesoura);
  and and_2 (and_2_out, not_1_out, papel, not_3_out);
  and and_3 (and_3_out, not_1_out, not_2_out, tesoura);
  and and_4 (and_4_out, pedra, not_2_out, not_3_out);
  or or_1 (S0, and_1_out, and_2_out);
  or or_2 (S1, and_3_out, and_4_out);
endmodule

module Modulo2 (
  input  Jog,
  input  I,
  input  Joga,
  input  II,
  output Sai,
  output da
);

  wire and_1_out, and_2_out, and_3_out, and_4_out, and_5_out, and_6_out, and_7_out, not_1_out, not_2_out,
       not_3_out, not_4_out;

  not not_1 (not_1_out, Jog);
  not not_2 (not_2_out, I);
  not not_3 (not_3_out, Joga);
  not not_4 (not_4_out, II);
  and and_1 (and_1_out, I, II);
  and and_2 (and_2_out, Jog, not_3_out, II);
  and and_3 (and_3_out, Jog, Joga, not_4_out);
  and and_4 (and_4_out, not_1_out, I, not_3_out, II);
  and and_5 (and_5_out, not_1_out, I, Joga, not_4_out);
  and and_6 (and_6_out, Jog, not_2_out, Joga);
  and and_7 (and_7_out, Jog, Joga, II);
  or or_1 (Sai, and_1_out, and_2_out, and_3_out);
  or or_2 (da, and_4_out, and_5_out, and_6_out, and_7_out);
endmodule

module Modulo3 (
  input  a,
  input  b,
  output VencedorJogardor1,
  output VencedorJogador2,
  output Empate
);

  wire not_1_out, not_2_out;

  not not_1 (not_1_out, a);
  not not_2 (not_2_out, b);
  and and_1 (VencedorJogardor1, a, not_2_out);
  and and_2 (VencedorJogador2, not_1_out, b);
  and and_3 (Empate, a, b);
endmodule
