// Logisim project trabalhoFinalJeffleyNicolas.circ as structural Verilog: 12 circuits, main circuit main
module main (
  input  [7:0] Entrada,
  input  [1:0] Rw,
  input  [1:0] Ra,
  input  [1:0] Rb,
  input  in_5,
  input  in_6,
  input  [2:0] SelectOperation,
  output out_8,
  output out_9
);

  wire [7:0] bancoregistradores_1_va, bancoregistradores_1_vb, leitornumerico_1_out_4, ula_1_s;

  leitorNumerico leitornumerico_1 (
    .selecionarValor(in_5), .valorEntrada(Entrada), .resultadoOperacao(ula_1_s),
    .out_4(leitornumerico_1_out_4));
  BancoRegistradores bancoregistradores_1 (
    .escrever(in_6), .RW(Rw), .VW(leitornumerico_1_out_4), .RA(Ra), .RB(Rb), .VA(bancoregistradores_1_va),
    .VB(bancoregistradores_1_vb));
  ULA ula_1 (
    .seletorOP(SelectOperation), .A(bancoregistradores_1_va), .B(bancoregistradores_1_vb), .C(out_8),
    .S(ula_1_s), .Z(out_9));
  LED led_1 (.in(ula_1_s[0]));
  LED led_2 (.in(ula_1_s[1]));
  LED led_3 (.in(ula_1_s[2]));
  LED led_4 (.in(ula_1_s[3]));
  LED led_5 (.in(ula_1_s[4]));
  LED led_6 (.in(ula_1_s[5]));
  LED led_7 (.in(ula_1_s[6]));
  LED led_8 (.in(ula_1_s[7]));

  // Notes on the sheet:
  //   100--div
  //   011-adi
  //   110--mult
  //   000--OR
  //   001--subs
  //   010--and
  //   101--xor
  //   0--para seleciona a Entrada
  //   1--para selecionar o valor da conta
  //   Z--caso resultado de 0
  //   C--overflow/underflow
  //   1
  //   2
  //   4
  //   8
  //   16
  //   32
  //   64
  //   selecionar registrador:
  //   00-- 1
  //   10--2
  //   01--3
  //   11--4
  //   128
endmodule

module SomadorSimples (
  input  numero1,
  input  numero2,
  input  restoSobe,
  output soma,
  output resto
);

  wire and_1_out, and_2_out, and_3_out, and_4_out, and_5_out, and_6_out, and_7_out, not_1_out, not_2_out,
       not_3_out;

  not not_1 (not_1_out, numero1);
  not not_2 (not_2_out, numero2);
  not not_3 (not_3_out, restoSobe);
  and and_1 (and_1_out, not_1_out, not_2_out, restoSobe);
  and and_2 (and_2_out, not_1_out, numero2, not_3_out);
  and and_3 (and_3_out, numero1, not_2_out, not_3_out);
  and and_4 (and_4_out, numero1, numero2, restoSobe);
  and and_5 (and_5_out, numero2, restoSobe);
  and and_6 (and_6_out, numero1, restoSobe);
  or or_1 (resto, and_5_out, and_6_out, and_7_out);
  and and_7 (and_7_out, numero1, numero2);
  or or_2 (soma, and_1_out, and_2_out, and_3_out, and_4_out);
endmodule

module SomadorCompleto (
  input  [7:0] Numero1,
  input  [7:0] Numero2,
  input  somaOUsubtracao,
  output overflow,
  output [7:0] resultado
);

  wire somadorsimples_1_resto, somadorsimples_2_resto, somadorsimples_3_resto, somadorsimples_4_resto,
       somadorsimples_5_resto, somadorsimples_6_resto, somadorsimples_7_resto, somadorsimples_8_resto,
       xor_1_out, xor_2_out, xor_3_out, xor_4_out, xor_5_out, xor_6_out, xor_7_out, xor_8_out;

  xor xor_1 (xor_1_out, somaOUsubtracao, Numero2[0]);
  xor xor_2 (xor_2_out, somaOUsubtracao, Numero2[1]);
  SomadorSimples somadorsimples_1 (
    .numero1(Numero1[0]), .numero2(xor_1_out), .restoSobe(somaOUsubtracao), .soma(resultado[0]),
    .resto(somadorsimples_1_resto));
  SomadorSimples somadorsimples_2 (
    .numero1(Numero1[1]), .numero2(xor_2_out), .restoSobe(somadorsimples_1_resto), .soma(resultado[1]),
    .resto(somadorsimples_2_resto));
  xor xor_3 (xor_3_out, somaOUsubtracao, Numero2[2]);
  SomadorSimples somadorsimples_3 (
    .numero1(Numero1[2]), .numero2(xor_3_out), .restoSobe(somadorsimples_2_resto), .soma(resultado[2]),
    .resto(somadorsimples_3_resto));
  xor xor_4 (xor_4_out, somaOUsubtracao, Numero2[3]);
  SomadorSimples somadorsimples_4 (
    .numero1(Numero1[3]), .numero2(xor_4_out), .restoSobe(somadorsimples_3_resto), .soma(resultado[3]),
    .resto(somadorsimples_4_resto));
  xor xor_5 (xor_5_out, somaOUsubtracao, Numero2[4]);
  SomadorSimples somadorsimples_5 (
    .numero1(Numero1[4]), .numero2(xor_5_out), .restoSobe(somadorsimples_4_resto), .soma(resultado[4]),
    .resto(somadorsimples_5_resto));
  xor xor_6 (xor_6_out, somaOUsubtracao, Numero2[5]);
  SomadorSimples somadorsimples_6 (
    .numero1(Numero1[5]), .numero2(xor_6_out), .restoSobe(somadorsimples_5_resto), .soma(resultado[5]),
    .resto(somadorsimples_6_resto));
  xor xor_7 (xor_7_out, somaOUsubtracao, Numero2[6]);
  SomadorSimples somadorsimples_7 (
    .numero1(Numero1[6]), .numero2(xor_7_out), .restoSobe(somadorsimples_6_resto), .soma(resultado[6]),
    .resto(somadorsimples_7_resto));
  xor xor_8 (xor_8_out, somaOUsubtracao, Numero2[7]);
  SomadorSimples somadorsimples_8 (
    .numero1(Numero1[7]), .numero2(xor_8_out), .restoSobe(somadorsimples_7_resto), .soma(resultado[7]),
    .resto(somadorsimples_8_resto));
  xor xor_9 (overflow, somadorsimples_8_resto, somadorsimples_7_resto);
endmodule

module ORR (
  input  [7:0] numero1,
  input  [7:0] numero2,
  output [7:0] out_3
);

  or or_1 (out_3[0], numero1[0], numero2[0]);
  or or_2 (out_3[1], numero1[1], numero2[1]);
  or or_3 (out_3[2], numero1[2], numero2[2]);
  or or_4 (out_3[3], numero1[3], numero2[3]);
  or or_5 (out_3[4], numero1[4], numero2[4]);
  or or_6 (out_3[5], numero1[5], numero2[5]);
  or or_7 (out_3[6], numero1[6], numero2[6]);
  or or_8 (out_3[7], numero1[7], numero2[7]);
endmodule

module ANDD (
  input  [7:0] numero1,
  input  [7:0] numero2,
  output [7:0] out_3
);

  and and_1 (out_3[0], numero1[0], numero2[0]);
  and and_2 (out_3[1], numero1[1], numero2[1]);
  and and_3 (out_3[2], numero1[2], numero2[2]);
  and and_4 (out_3[3], numero1[3], numero2[3]);
  and and_5 (out_3[4], numero1[4], numero2[4]);
  and and_6 (out_3[5], numero1[5], numero2[5]);
  and and_7 (out_3[6], numero1[6], numero2[6]);
  and and_8 (out_3[7], numero1[7], numero2[7]);
endmodule

module XORR (
  input  [7:0] numero1,
  input  [7:0] numero2,
  output [7:0] out_3
);

  xor xor_1 (out_3[0], numero1[0], numero2[0]);
  xor xor_2 (out_3[1], numero1[1], numero2[1]);
  xor xor_3 (out_3[2], numero1[2], numero2[2]);
  xor xor_4 (out_3[3], numero1[3], numero2[3]);
  xor xor_5 (out_3[4], numero1[4], numero2[4]);
  xor xor_6 (out_3[5], numero1[5], numero2[5]);
  xor xor_7 (out_3[6], numero1[6], numero2[6]);
  xor xor_8 (out_3[7], numero1[7], numero2[7]);
endmodule

module leitorNumerico (
  input  [7:0] valorEntrada,
  input  [7:0] resultadoOperacao,
  input  selecionarValor,
  output [7:0] out_4
);

  wire [7:0] and_1_out, and_2_out;

  assign and_1_out = valorEntrada & ~{8{selecionarValor}};  // AND_Gate and_1, 8 bits wide
  assign and_2_out = resultadoOperacao & {8{selecionarValor}};  // AND_Gate and_2, 8 bits wide
  assign out_4 = and_1_out | and_2_out;  // OR_Gate or_1, 8 bits wide
endmodule

module registrador (
  input  [7:0] in_1,
  input  in_2,
  output [7:0] out_3
);

  D_Flip_Flop d_ff_1 (.D(in_1[0]), .clk(in_2), .Q(out_3[0]));  // open: Qn, preset, reset
  D_Flip_Flop d_ff_2 (.D(in_1[1]), .clk(in_2), .Q(out_3[1]));  // open: Qn, preset, reset
  D_Flip_Flop d_ff_3 (.D(in_1[2]), .clk(in_2), .Q(out_3[2]));  // open: Qn, preset, reset
  D_Flip_Flop d_ff_4 (.D(in_1[3]), .clk(in_2), .Q(out_3[3]));  // open: Qn, preset, reset
  D_Flip_Flop d_ff_5 (.D(in_1[4]), .clk(in_2), .Q(out_3[4]));  // open: Qn, preset, reset
  D_Flip_Flop d_ff_6 (.D(in_1[5]), .clk(in_2), .Q(out_3[5]));  // open: Qn, preset, reset
  D_Flip_Flop d_ff_7 (.D(in_1[6]), .clk(in_2), .Q(out_3[6]));  // open: Qn, preset, reset
  D_Flip_Flop d_ff_8 (.D(in_1[7]), .clk(in_2), .Q(out_3[7]));  // open: Qn, preset, reset
endmodule

module SeletorRegistrador (
  input  a,
  input  b,
  output R0,
  output R1,
  output R2,
  output R3
);

  wire not_1_out, not_2_out;

  not not_1 (not_1_out, a);
  not not_2 (not_2_out, b);
  and and_1 (R0, not_1_out, not_2_out);
  and and_2 (R1, not_1_out, b);
  and and_3 (R2, a, not_2_out);
  and and_4 (R3, a, b);
endmodule

module BancoRegistradores (
  input  [7:0] VW,
  input  [1:0] RW,
  input  escrever,
  input  [1:0] RA,
  input  [1:0] RB,
  output [7:0] VA,
  output [7:0] VB
);

  wire controlled_buffer_1_out, controlled_buffer_2_out, controlled_buffer_3_out, controlled_buffer_4_out,
       seletorregistrador_1_r0, seletorregistrador_1_r1, seletorregistrador_1_r2, seletorregistrador_1_r3,
       seletorregistrador_2_r0, seletorregistrador_2_r1, seletorregistrador_2_r2, seletorregistrador_2_r3,
       seletorregistrador_3_r0, seletorregistrador_3_r1, seletorregistrador_3_r2, seletorregistrador_3_r3;
  wire [7:0] registrador_1_out_3, registrador_2_out_3, registrador_3_out_3, registrador_4_out_3;

  SeletorRegistrador seletorregistrador_1 (
    .a(RW[0]), .b(RW[1]), .R0(seletorregistrador_1_r0), .R1(seletorregistrador_1_r1),
    .R2(seletorregistrador_1_r2), .R3(seletorregistrador_1_r3));
  assign controlled_buffer_1_out = escrever ? seletorregistrador_1_r0 : 1'bz;  // Controlled_Buffer controlled_buffer_1
  assign controlled_buffer_2_out = escrever ? seletorregistrador_1_r1 : 1'bz;  // Controlled_Buffer controlled_buffer_2
  assign controlled_buffer_3_out = escrever ? seletorregistrador_1_r2 : 1'bz;  // Controlled_Buffer controlled_buffer_3
  assign controlled_buffer_4_out = escrever ? seletorregistrador_1_r3 : 1'bz;  // Controlled_Buffer controlled_buffer_4
  registrador registrador_1 (.in_1(VW), .in_2(controlled_buffer_1_out), .out_3(registrador_1_out_3));
  registrador registrador_2 (.in_1(VW), .in_2(controlled_buffer_2_out), .out_3(registrador_2_out_3));
  registrador registrador_3 (.in_1(VW), .in_2(controlled_buffer_3_out), .out_3(registrador_3_out_3));
  registrador registrador_4 (.in_1(VW), .in_2(controlled_buffer_4_out), .out_3(registrador_4_out_3));
  assign VA = seletorregistrador_2_r0 ? registrador_1_out_3 : 8'bz;  // Controlled_Buffer controlled_buffer_5
  assign VB = seletorregistrador_3_r0 ? registrador_1_out_3 : 8'bz;  // Controlled_Buffer controlled_buffer_6
  assign VA = seletorregistrador_2_r1 ? registrador_2_out_3 : 8'bz;  // Controlled_Buffer controlled_buffer_7
  assign VB = seletorregistrador_3_r1 ? registrador_2_out_3 : 8'bz;  // Controlled_Buffer controlled_buffer_8
  assign VA = seletorregistrador_2_r2 ? registrador_3_out_3 : 8'bz;  // Controlled_Buffer controlled_buffer_9
  assign VB = seletorregistrador_3_r2 ? registrador_3_out_3 : 8'bz;  // Controlled_Buffer controlled_buffer_10
  assign VA = seletorregistrador_2_r3 ? registrador_4_out_3 : 8'bz;  // Controlled_Buffer controlled_buffer_11
  assign VB = seletorregistrador_3_r3 ? registrador_4_out_3 : 8'bz;  // Controlled_Buffer controlled_buffer_12
  SeletorRegistrador seletorregistrador_2 (
    .a(RA[0]), .b(RA[1]), .R0(seletorregistrador_2_r0), .R1(seletorregistrador_2_r1),
    .R2(seletorregistrador_2_r2), .R3(seletorregistrador_2_r3));
  SeletorRegistrador seletorregistrador_3 (
    .a(RB[0]), .b(RB[1]), .R0(seletorregistrador_3_r0), .R1(seletorregistrador_3_r1),
    .R2(seletorregistrador_3_r2), .R3(seletorregistrador_3_r3));
endmodule

module ULA (
  input  [2:0] seletorOP,
  input  [7:0] A,
  input  [7:0] B,
  output [7:0] S,
  output Z,
  output C
);

  wire and_1_out, and_2_out, and_3_out, and_4_out, and_5_out, and_6_out, and_7_out, and_8_out, not_1_out,
       not_2_out, not_3_out, not_4_out, somadorcompleto_1_overflow;
  wire [7:0] andd_1_out_3, controlled_buffer_1_out, controlled_buffer_2_out, controlled_buffer_3_out,
       controlled_buffer_5_out, controlled_buffer_7_out, controlled_buffer_8_out, controlled_buffer_9_out,
       controlled_buffer_10_out, controlled_buffer_12_out, controlled_buffer_13_out,
       controlled_buffer_16_out, controlled_buffer_17_out, controlled_buffer_19_out,
       controlled_buffer_20_out, controlled_buffer_24_out, divider_1_out, multiplier_1_cout,
       multiplier_1_out, norr_1_out_3, orr_1_out_3, somadorcompleto_1_resultado, xorr_1_out_3;

  not not_1 (not_1_out, seletorOP[2]);
  not not_2 (not_2_out, seletorOP[1]);
  not not_3 (not_3_out, seletorOP[0]);
  and and_1 (and_1_out, not_1_out, not_2_out, not_3_out);
  and and_2 (and_2_out, not_1_out, not_2_out, seletorOP[0]);
  and and_3 (and_3_out, not_1_out, seletorOP[1], not_3_out);
  and and_4 (and_4_out, not_1_out, seletorOP[1], seletorOP[0]);
  and and_5 (and_5_out, seletorOP[2], not_2_out, not_3_out);
  and and_6 (and_6_out, seletorOP[2], not_2_out, seletorOP[0]);
  and and_7 (and_7_out, seletorOP[2], seletorOP[1], not_3_out);
  and and_8 (and_8_out, seletorOP[2], seletorOP[1], seletorOP[0]);
  assign controlled_buffer_1_out = and_1_out ? A : 8'bz;  // Controlled_Buffer controlled_buffer_1
  assign controlled_buffer_2_out = and_1_out ? B : 8'bz;  // Controlled_Buffer controlled_buffer_2
  assign controlled_buffer_3_out = and_2_out ? A : 8'bz;  // Controlled_Buffer controlled_buffer_3
  assign controlled_buffer_3_out = and_4_out ? A : 8'bz;  // Controlled_Buffer controlled_buffer_4
  assign controlled_buffer_5_out = and_2_out ? B : 8'bz;  // Controlled_Buffer controlled_buffer_5
  assign controlled_buffer_5_out = and_4_out ? B : 8'bz;  // Controlled_Buffer controlled_buffer_6
  SomadorCompleto somadorcompleto_1 (
    .Numero1(controlled_buffer_3_out), .Numero2(controlled_buffer_5_out), .somaOUsubtracao(and_2_out),
    .overflow(somadorcompleto_1_overflow), .resultado(somadorcompleto_1_resultado));
  assign controlled_buffer_7_out = and_5_out ? A : 8'bz;  // Controlled_Buffer controlled_buffer_7
  assign controlled_buffer_8_out = and_5_out ? B : 8'bz;  // Controlled_Buffer controlled_buffer_8
  assign controlled_buffer_9_out = and_3_out ? B : 8'bz;  // Controlled_Buffer controlled_buffer_9
  ORR orr_1 (.numero1(controlled_buffer_1_out), .numero2(controlled_buffer_2_out), .out_3(orr_1_out_3));
  Divider divider_1 (
    .a(controlled_buffer_7_out), .b(controlled_buffer_8_out), .out(divider_1_out));  // open: upper, rem
  assign controlled_buffer_10_out = and_3_out ? A : 8'bz;  // Controlled_Buffer controlled_buffer_10
  assign S = and_1_out ? orr_1_out_3 : 8'bz;  // Controlled_Buffer controlled_buffer_11
  assign controlled_buffer_12_out = and_8_out ? A : 8'bz;  // Controlled_Buffer controlled_buffer_12
  assign controlled_buffer_13_out = and_8_out ? B : 8'bz;  // Controlled_Buffer controlled_buffer_13
  assign S = and_4_out ? somadorcompleto_1_resultado : 8'bz;  // Controlled_Buffer controlled_buffer_14
  assign S = and_5_out ? divider_1_out : 8'bz;  // Controlled_Buffer controlled_buffer_15
  assign controlled_buffer_16_out = and_6_out ? A : 8'bz;  // Controlled_Buffer controlled_buffer_16
  assign controlled_buffer_17_out = and_6_out ? B : 8'bz;  // Controlled_Buffer controlled_buffer_17
  assign S = and_2_out ? somadorcompleto_1_resultado : 8'bz;  // Controlled_Buffer controlled_buffer_18
  assign controlled_buffer_19_out = and_7_out ? A : 8'bz;  // Controlled_Buffer controlled_buffer_19
  assign controlled_buffer_20_out = and_7_out ? B : 8'bz;  // Controlled_Buffer controlled_buffer_20
  assign S = and_3_out ? andd_1_out_3 : 8'bz;  // Controlled_Buffer controlled_buffer_21
  ANDD andd_1 (.numero1(controlled_buffer_10_out), .numero2(controlled_buffer_9_out), .out_3(andd_1_out_3));
  Multiplier multiplier_1 (
    .a(controlled_buffer_19_out), .b(controlled_buffer_20_out), .out(multiplier_1_out),
    .cout(multiplier_1_cout));  // open: cin
  XORR xorr_1 (.numero1(controlled_buffer_16_out), .numero2(controlled_buffer_17_out), .out_3(xorr_1_out_3));
  assign S = and_7_out ? multiplier_1_out : 8'bz;  // Controlled_Buffer controlled_buffer_22
  not not_4 (not_4_out, and_7_out);
  NORR norr_1 (.numero1(controlled_buffer_12_out), .numero2(controlled_buffer_13_out), .out_3(norr_1_out_3));
  assign S = and_6_out ? xorr_1_out_3 : 8'bz;  // Controlled_Buffer controlled_buffer_23
  assign controlled_buffer_24_out = and_7_out ? multiplier_1_cout : 8'bz;  // Controlled_Buffer controlled_buffer_24
  assign controlled_buffer_24_out = not_4_out ? {8{1'b0}} : 8'bz;  // Controlled_Buffer controlled_buffer_25
  assign S = and_8_out ? norr_1_out_3 : 8'bz;  // Controlled_Buffer controlled_buffer_26
  or or_1 (C, somadorcompleto_1_overflow, controlled_buffer_24_out[0], controlled_buffer_24_out[1], controlled_buffer_24_out[2], controlled_buffer_24_out[3], controlled_buffer_24_out[4], controlled_buffer_24_out[5], controlled_buffer_24_out[6], controlled_buffer_24_out[7]);
  nor nor_1 (Z, S[0], S[1], S[2], S[3], S[4], S[5], S[6], S[7]);

  // Notes on the sheet:
  //   Seletor de Operecao
  //   multiplicação
  //   OR
  //   subtração
  //   adição
  //   divisão
  //   AND
  //   XOR
endmodule

module NORR (
  input  [7:0] numero1,
  input  [7:0] numero2,
  output [7:0] out_3
);

  nor nor_1 (out_3[0], numero1[0], numero2[0]);
  nor nor_2 (out_3[1], numero1[1], numero2[1]);
  nor nor_3 (out_3[2], numero1[2], numero2[2]);
  nor nor_4 (out_3[3], numero1[3], numero2[3]);
  nor nor_5 (out_3[4], numero1[4], numero2[4]);
  nor nor_6 (out_3[5], numero1[5], numero2[5]);
  nor nor_7 (out_3[6], numero1[6], numero2[6]);
  nor nor_8 (out_3[7], numero1[7], numero2[7]);
endmodule
